// Logisim project Lab01_Mux21.circ as structural Verilog: 1 circuit, main circuit main
module main (
  input  Sel,
  input  In1,
  input  In2,
  output Out1
);

  wire and_1_out, and_2_out, not_1_out, not_2_out;

  not not_1 (not_1_out, Sel);
  not not_2 (not_2_out, not_1_out);
  and and_1 (and_1_out, not_2_out, In1);
  and and_2 (and_2_out, not_1_out, In2);
  or or_1 (Out1, and_1_out, and_2_out);

  // Notes on the sheet:
  //   Kenzhegul Nurbol
  //   Lab 01: 2-Way, 1-Bit mmultiplexer
  //   Feburary 26, 2024
endmodule
