// Logisim project Lab03_Encoder.circ as structural Verilog: 2 circuits, main circuit main
module main (
  input  In1,
  input  In2,
  input  In3,
  input  In4,
  input  In5,
  input  In6,
  input  In7,
  input  In8,
  input  In9,
  output [3:0] PriOut
);

  Encoder encoder_1 (
    .In1(In1), .In2(In2), .In3(In3), .In4(In4), .In5(In5), .In6(In6), .In7(In7), .In8(In8), .In9(In9),
    .Out1(PriOut[0]), .Out2(PriOut[1]), .Out3(PriOut[2]), .Out4(PriOut[3]));
  Hex_Digit_Display hex_digit_display_1 (.value(PriOut));  // open: dp

  // Notes on the sheet:
  //   March 03, 2024
  //   Kenzhegul Nurbol
  //   Lab 03: Nine-Line Priority Encoder
endmodule

module Encoder (
  input  In1,
  input  In2,
  input  In3,
  input  In4,
  input  In5,
  input  In6,
  input  In7,
  input  In8,
  input  In9,
  output Out1,
  output Out2,
  output Out3,
  output Out4
);

  wire U1_out, U2_out, U3_out, U4_out, U5_out, U6_out, U7_out, U8_out, U9_out, U10_out, U11_out, U12_out,
       U16_out;

  nor U16 (U16_out, In8, In9);
  and U1 (U1_out, In1, ~In2, ~In4, ~In6, U16_out);  // AND_Gate
  and U2 (U2_out, In3, ~In4, ~In6, U16_out);  // AND_Gate
  and U3 (U3_out, In5, ~In6, U16_out);  // AND_Gate
  or U13 (Out1, U1_out, U2_out, U3_out, U4_out, In9);
  and U4 (U4_out, In7, U16_out);
  and U5 (U5_out, In2, ~In4, ~In5, U16_out);  // AND_Gate
  and U6 (U6_out, ~In4, ~In5, In3, U16_out);  // AND_Gate
  or U14 (Out2, U5_out, U6_out, U7_out, U8_out);
  and U7 (U7_out, In6, U16_out);
  and U8 (U8_out, In7, U16_out);
  and U9 (U9_out, In4, U16_out);
  and U10 (U10_out, In5, U16_out);
  or U15 (Out3, U9_out, U10_out, U11_out, U12_out);
  and U11 (U11_out, In6, U16_out);
  and U12 (U12_out, In7, U16_out);
  or U17 (Out4, In9, In8);

  // Notes on the sheet:
  //   March 03, 2024
  //   Kenzhegul Nurbol
  //   Lab 03: Nine-Line Priority Encoder
endmodule
